# Fritzing sketch Orologio Emotivo Frizzing (saved by Fritzing 1.0.1rc)
breadboards: 1

parts:
  ZS-042_RTC1 = ZS-042 RTC Module
  Componente1 = Arduino Uno (Rev3)
  R1 = Resistor [tolerance=±5% power=0.25W resistance=220 package=THT]
  R2 = Resistor [tolerance=±5% power=0.25W resistance=220 package=THT]
  LCD1 = LCD screen
  J1 = Piezo Speaker

nets:
  GND: ZS-042_RTC1.GND, Componente1.GND, R1.Pin_0, LCD1.VSS, LCD1.R/W, LCD1.LED-, J1.pin1
  VCC: ZS-042_RTC1.VCC, Componente1.5V, R2.Pin_0, LCD1.VDD
  N1: ZS-042_RTC1.SDA, Componente1.A4/SDA
  N2: ZS-042_RTC1.SCL, Componente1.A5/SCL
  N3: Componente1.D9_PWM, LCD1.DB4
  N4: Componente1.D10_PWM/SS, LCD1.DB5
  N5: Componente1.D11_PWM/MOSI, LCD1.DB6
  N6: Componente1.D12/MISO, LCD1.DB7
  N7: Componente1.D13/SCK, J1.pin2
  N8: Componente1.D3_PWM, LCD1.RS
  N9: Componente1.D5_PWM, LCD1.E
  N10: R1.Pin_1, LCD1.V0
  N11: R2.Pin_1, LCD1.LED+
